// Logisim project mips_pipeline.circ as structural Verilog: 20 circuits, main circuit main
module main (
);

  wire clock_1_out, decide_branch_1_is_branch, hazard_detection_unit_1_clear_id_ex,
       hazard_detection_unit_1_enable_if_id, hazard_detection_unit_1_enable_pc, reg_ex_mem_1_branch_2,
       reg_ex_mem_1_memory_write_2, reg_ex_mem_1_memtoreg_2, reg_ex_mem_1_regwrite_2, reg_ex_mem_1_zero_2,
       reg_id_ex_1_alusrc_2, reg_id_ex_1_branch_2, reg_id_ex_1_jr_2, reg_id_ex_1_jump_2,
       reg_id_ex_1_memtoreg_2, reg_id_ex_1_memwrite_2, reg_id_ex_1_regdest_2, reg_id_ex_1_regwrite_2,
       reg_mem_wb_1_memtoreg_2, reg_mem_wb_1_reg_write_2, uc_w_1_alusrc, uc_w_1_branch, uc_w_1_jr,
       uc_w_1_jump, uc_w_1_memtoreg, uc_w_1_memwrite, uc_w_1_regdest, uc_w_1_regwrite, ula_1_igual;
  wire [1:0] forwarding_unit_1_forward_a, forwarding_unit_1_forward_b;
  wire [2:0] reg_ex_mem_1_aluop_2, reg_id_ex_1_aluop_2, uc_w_1_aluop;
  wire [4:0] alu_mux_control_1_shift_amount, instruction_decomposition_1_rd, instruction_decomposition_1_rs,
       instruction_decomposition_1_rs_2, instruction_decomposition_1_rt, instruction_decomposition_1_rt_2,
       instruction_decomposition_1_shamt, reg_ex_mem_1_write_register_2, reg_id_ex_1_rd_2, reg_id_ex_1_rs_2,
       reg_id_ex_1_rt_2, reg_id_ex_1_shamt_2, reg_mem_wb_1_write_register_2, wr_out_select_1_wr_register;
  wire [5:0] alu_control_1_ula_op, instruction_decomposition_1_func, instruction_decomposition_1_opcode,
       reg_id_ex_1_func_2;
  wire [15:0] pc_select_1__16_bits;
  wire [25:0] instruction_decomposition_1_label, reg_id_ex_1_label_2;
  wire [31:0] alu_mux_control_1_a, alu_mux_control_1_b, alu_mux_control_1_data_rt_2,
       banco_registradores_1_r1, banco_registradores_1_r2, DATA_MEMORY_data, forwarding_unit_2_1_data_rs,
       forwarding_unit_2_1_data_rt, instruction_decomposition_1_imext, INSTRUCTION_MEMORY_data,
       multiplexer_1_out, pc_encode_1_branch_address, pc_encode_1_jump_address, pc_select_1_pc_4_2,
       reg_ex_mem_1_alu_out_2, reg_ex_mem_1_branch_address_2, reg_ex_mem_1_data_rt_2, reg_id_ex_1_data_rs_2,
       reg_id_ex_1_data_rt_2, reg_id_ex_1_imext_2, reg_id_ex_1_pc_4_2, reg_if_id_1_instruction_2,
       reg_if_id_1_pc_4_2, reg_mem_wb_1_alu_out_2, reg_mem_wb_1_mem_out_2, ula_1_resultado,
       wr_out_select_1_alu_out;

  PC_SELECT pc_select_1 (
    .JR(reg_id_ex_1_jr_2), .JUMP(reg_id_ex_1_jump_2), .BRANCH(decide_branch_1_is_branch),
    .PC_4_2(pc_select_1_pc_4_2), ._16_BITS(pc_select_1__16_bits), .PC_BRANCH(reg_ex_mem_1_branch_address_2),
    .PC_JUMP(pc_encode_1_jump_address), .PC_JR(reg_id_ex_1_data_rs_2), .PC_4(pc_select_1_pc_4_2),
    .CLK(clock_1_out), .in_8(hazard_detection_unit_1_enable_pc));
  RAM #(.addrWidth(16), .dataWidth(32), .Select("high"), .simpleMode("false")) INSTRUCTION_MEMORY (
    .addr(pc_select_1__16_bits), .data(INSTRUCTION_MEMORY_data), .clk(clock_1_out));  // open: sel, ld, clr
  Clock clock_1 (.out(clock_1_out));
  REG_IF_ID reg_if_id_1 (
    .PC_4(pc_select_1_pc_4_2), .INSTRUCTION(INSTRUCTION_MEMORY_data), .PC_4_2(reg_if_id_1_pc_4_2),
    .INSTRUCTION_2(reg_if_id_1_instruction_2), .CLK(clock_1_out), .in_3(hazard_detection_unit_1_enable_if_id));
  INSTRUCTION_DECOMPOSITION instruction_decomposition_1 (
    .in_1(reg_if_id_1_instruction_2), .OPCODE(instruction_decomposition_1_opcode),
    .LABEL(instruction_decomposition_1_label), .RS(instruction_decomposition_1_rs),
    .RT(instruction_decomposition_1_rt), .RD(instruction_decomposition_1_rd),
    .SHAMT(instruction_decomposition_1_shamt), .FUNC(instruction_decomposition_1_func),
    .IMEXT(instruction_decomposition_1_imext), .RT_2(instruction_decomposition_1_rt_2),
    .RS_2(instruction_decomposition_1_rs_2));
  banco_registradores banco_registradores_1 (
    .R1_num(instruction_decomposition_1_rs), .R2_num(instruction_decomposition_1_rt),
    .RW(reg_mem_wb_1_write_register_2), .Din(multiplexer_1_out), .WE(reg_mem_wb_1_reg_write_2),
    .clk(clock_1_out), .R1(banco_registradores_1_r1), .R2(banco_registradores_1_r2));
  UC_W uc_w_1 (
    .in_1(instruction_decomposition_1_opcode), .REGDEST(uc_w_1_regdest), .JUMP(uc_w_1_jump),
    .BRANCH(uc_w_1_branch), .MEMTOREG(uc_w_1_memtoreg), .ALUOP(uc_w_1_aluop), .MEMWRITE(uc_w_1_memwrite),
    .ALUSRC(uc_w_1_alusrc), .REGWRITE(uc_w_1_regwrite), .JR(uc_w_1_jr));
  FORWARDING_UNIT_2 forwarding_unit_2_1 (
    .R1(banco_registradores_1_r1), .R2(banco_registradores_1_r2), .RS(instruction_decomposition_1_rs_2),
    .RT(instruction_decomposition_1_rt_2), .DATA_RS(forwarding_unit_2_1_data_rs),
    .DATA_RT(forwarding_unit_2_1_data_rt), .WR(reg_mem_wb_1_reg_write_2),
    .REG_DEST(reg_mem_wb_1_write_register_2), .WRITE_DATA(multiplexer_1_out));
  HAZARD_DETECTION_UNIT hazard_detection_unit_1 (
    .ENABLE_PC(hazard_detection_unit_1_enable_pc), .ENABLE_IF_ID(hazard_detection_unit_1_enable_if_id),
    .CLEAR_ID_EX(hazard_detection_unit_1_clear_id_ex), .IFID_rt(instruction_decomposition_1_rt_2),
    .IFID_rs(instruction_decomposition_1_rs_2), .IDEX_rt(reg_id_ex_1_rt_2),
    .IDEX_MemRead(reg_id_ex_1_memtoreg_2));
  REG_ID_EX reg_id_ex_1 (
    .RegDest(uc_w_1_regdest), .Branch(uc_w_1_branch), .MemtoReg(uc_w_1_memtoreg), .ALUOp(uc_w_1_aluop),
    .ALUSrc(uc_w_1_alusrc), .RegWrite(uc_w_1_regwrite), .PC_4(reg_if_id_1_pc_4_2),
    .DATA_RS(forwarding_unit_2_1_data_rs), .DATA_RT(forwarding_unit_2_1_data_rt),
    .IMEXT(instruction_decomposition_1_imext), .RT(instruction_decomposition_1_rt_2),
    .RD(instruction_decomposition_1_rd), .RegDest_2(reg_id_ex_1_regdest_2), .Branch_2(reg_id_ex_1_branch_2),
    .MemtoReg_2(reg_id_ex_1_memtoreg_2), .ALUOp_2(reg_id_ex_1_aluop_2), .ALUSrc_2(reg_id_ex_1_alusrc_2),
    .RegWrite_2(reg_id_ex_1_regwrite_2), .PC_4_2(reg_id_ex_1_pc_4_2), .DATA_RS_2(reg_id_ex_1_data_rs_2),
    .DATA_RT_2(reg_id_ex_1_data_rt_2), .IMEXT_2(reg_id_ex_1_imext_2), .RT_2(reg_id_ex_1_rt_2),
    .RD_2(reg_id_ex_1_rd_2), .CLK(clock_1_out), .MemWrite(uc_w_1_memwrite),
    .MemWrite_2(reg_id_ex_1_memwrite_2), .LABEL(instruction_decomposition_1_label),
    .LABEL_2(reg_id_ex_1_label_2), .Jump(uc_w_1_jump), .Jump_2(reg_id_ex_1_jump_2), .Jr(uc_w_1_jr),
    .Jr_2(reg_id_ex_1_jr_2), .SHAMT(instruction_decomposition_1_shamt), .SHAMT_2(reg_id_ex_1_shamt_2),
    .FUNC(instruction_decomposition_1_func), .FUNC_2(reg_id_ex_1_func_2),
    .RS(instruction_decomposition_1_rs_2), .RS_2(reg_id_ex_1_rs_2),
    .CLEAR(hazard_detection_unit_1_clear_id_ex));
  FORWARDING_UNIT forwarding_unit_1 (
    .FORWARD_A(forwarding_unit_1_forward_a), .FORWARD_B(forwarding_unit_1_forward_b),
    .IDEX_RT(reg_id_ex_1_rt_2), .ID_EX_RS(reg_id_ex_1_rs_2), .EX_MEM_RD(reg_ex_mem_1_write_register_2),
    .EX_MEM_REG_WRITE(reg_ex_mem_1_regwrite_2), .MEM_WB_RD(reg_mem_wb_1_write_register_2),
    .MEM_WB_REG_WRITE(reg_mem_wb_1_reg_write_2));
  ALU_MUX_CONTROL alu_mux_control_1 (
    .DATA_RS(reg_id_ex_1_data_rs_2), .DATA_RT(reg_id_ex_1_data_rt_2), .SHAMT(reg_id_ex_1_shamt_2),
    .IMEXT(reg_id_ex_1_imext_2), .EX_MEM_RESULT(reg_ex_mem_1_alu_out_2), .MEM_WB_RESULT(multiplexer_1_out),
    .A(alu_mux_control_1_a), .B(alu_mux_control_1_b), .SHIFT_AMOUNT(alu_mux_control_1_shift_amount),
    .FORWARD_A(forwarding_unit_1_forward_a), .FORWARD_B(forwarding_unit_1_forward_b),
    .ALU_SRC(reg_id_ex_1_alusrc_2), .DATA_RT_2(alu_mux_control_1_data_rt_2));
  ULA ula_1 (
    .A(alu_mux_control_1_a), .B(alu_mux_control_1_b), .Resultado(ula_1_resultado), .OP(alu_control_1_ula_op),
    .igual(ula_1_igual), .SHIFT_AMOUNT(alu_mux_control_1_shift_amount));
  ALU_CONTROL alu_control_1 (.FUNC(reg_id_ex_1_func_2), .ULA_OP(alu_control_1_ula_op), .ALU_OP(reg_id_ex_1_aluop_2));
  PC_ENCODE pc_encode_1 (
    .LABEL(reg_id_ex_1_label_2), .PC_4(reg_id_ex_1_pc_4_2), .IMEXT(reg_id_ex_1_imext_2),
    .JUMP_ADDRESS(pc_encode_1_jump_address), .BRANCH_ADDRESS(pc_encode_1_branch_address));
  REG_EX_MEM reg_ex_mem_1 (
    .BRANCH(reg_id_ex_1_branch_2), .MEMTOREG(reg_id_ex_1_memtoreg_2), .MEMORY_WRITE(reg_id_ex_1_memwrite_2),
    .REGWRITE(reg_id_ex_1_regwrite_2), .BRANCH_ADDRESS(pc_encode_1_branch_address), .zero(ula_1_igual),
    .ALU_OUT(wr_out_select_1_alu_out), .DATA_RT(alu_mux_control_1_data_rt_2),
    .WRITE_REGISTER(wr_out_select_1_wr_register), .BRANCH_2(reg_ex_mem_1_branch_2),
    .MEMTOREG_2(reg_ex_mem_1_memtoreg_2), .MEMORY_WRITE_2(reg_ex_mem_1_memory_write_2),
    .REGWRITE_2(reg_ex_mem_1_regwrite_2), .BRANCH_ADDRESS_2(reg_ex_mem_1_branch_address_2),
    .zero_2(reg_ex_mem_1_zero_2), .ALU_OUT_2(reg_ex_mem_1_alu_out_2), .DATA_RT_2(reg_ex_mem_1_data_rt_2),
    .WRITE_REGISTER_2(reg_ex_mem_1_write_register_2), .CLK(clock_1_out), .ALUOP(reg_id_ex_1_aluop_2),
    .ALUOP_2(reg_ex_mem_1_aluop_2));
  WR_OUT_SELECT wr_out_select_1 (
    .RT(reg_id_ex_1_rt_2), .RD(reg_id_ex_1_rd_2), .WR_REGISTER(wr_out_select_1_wr_register),
    .JUMP(reg_id_ex_1_jump_2), .REG_DEST(reg_id_ex_1_regdest_2), .PC_4(reg_id_ex_1_pc_4_2),
    .AUL_RESULT(ula_1_resultado), .ALU_OUT(wr_out_select_1_alu_out));
  DECIDE_BRANCH decide_branch_1 (
    .ZERO(reg_ex_mem_1_zero_2), .ALU_OP(reg_ex_mem_1_aluop_2), .BRANCH(reg_ex_mem_1_branch_2),
    .IS_BRANCH(decide_branch_1_is_branch));
  RAM #(.addrWidth(16), .dataWidth(32), .bus("separate"), .Select("high"), .simpleMode("false")) DATA_MEMORY (
    .addr(reg_ex_mem_1_alu_out_2[17:2]), .din(reg_ex_mem_1_data_rt_2), .data(DATA_MEMORY_data),
    .str(reg_ex_mem_1_memory_write_2), .clk(clock_1_out));  // open: sel, ld, clr
  REG_MEM_WB reg_mem_wb_1 (
    .REG_WRITE(reg_ex_mem_1_regwrite_2), .MEMTOREG(reg_ex_mem_1_memtoreg_2), .MEM_OUT(DATA_MEMORY_data),
    .ALU_OUT(reg_ex_mem_1_alu_out_2), .WRITE_REGISTER(reg_ex_mem_1_write_register_2),
    .REG_WRITE_2(reg_mem_wb_1_reg_write_2), .MEMTOREG_2(reg_mem_wb_1_memtoreg_2),
    .MEM_OUT_2(reg_mem_wb_1_mem_out_2), .ALU_OUT_2(reg_mem_wb_1_alu_out_2),
    .WRITE_REGISTER_2(reg_mem_wb_1_write_register_2), .CLK(clock_1_out));
  Multiplexer #(.width(32), .enable("false")) multiplexer_1 (
    .in0(reg_mem_wb_1_alu_out_2), .in1(reg_mem_wb_1_mem_out_2), .out(multiplexer_1_out),
    .sel(reg_mem_wb_1_memtoreg_2));
endmodule

module banco_registradores (
  input  [4:0] R1_num,
  input  [4:0] R2_num,
  input  [4:0] RW,
  input  [31:0] Din,
  input  WE,
  input  clk,
  output [31:0] R1,
  output [31:0] R2
);

  wire demultiplexer_1_out0, demultiplexer_1_out1, demultiplexer_1_out2, demultiplexer_1_out3,
       demultiplexer_2_out0, demultiplexer_2_out1, demultiplexer_2_out2, demultiplexer_2_out3,
       demultiplexer_2_out4, demultiplexer_2_out5, demultiplexer_2_out6, demultiplexer_2_out7,
       demultiplexer_3_out0, demultiplexer_3_out1, demultiplexer_3_out2, demultiplexer_3_out3,
       demultiplexer_3_out4, demultiplexer_3_out5, demultiplexer_3_out6, demultiplexer_3_out7,
       demultiplexer_4_out0, demultiplexer_4_out1, demultiplexer_4_out2, demultiplexer_4_out3,
       demultiplexer_4_out4, demultiplexer_4_out5, demultiplexer_4_out6, demultiplexer_4_out7,
       demultiplexer_5_out0, demultiplexer_5_out1, demultiplexer_5_out2, demultiplexer_5_out3,
       demultiplexer_5_out4, demultiplexer_5_out5, demultiplexer_5_out6, demultiplexer_5_out7;
  wire [31:0] _0__Zero_q, _1__at_q, _3__v1_q, _5__a1_q, _6__a2_q, _7__a3_q, _8__t0_q, _9__t1_q, _10__t2_q,
       _11__t3_q, _12__t4_q, _13__t5_q, _14__t6_q, _15__t7_q, _19__s3_q, _20__s4_q, _21__s5_q, _22__s6_q,
       _23__s7_q, _24__t8_q, _25__t9_q, _26__k0_q, _27__k1_q, _28__gp_q, _29__sp_q, _30__fp_q, a0, ra, s0,
       s1, s2, v0;

  Demultiplexer #(.select(2), .disabled(0)) demultiplexer_1 (
    .out0(demultiplexer_1_out0), .out1(demultiplexer_1_out1), .out2(demultiplexer_1_out2),
    .out3(demultiplexer_1_out3), .in(1'b1), .sel(RW[4:3]), .en(WE));
  Demultiplexer #(.select(3), .disabled(0)) demultiplexer_2 (
    .out0(demultiplexer_2_out0), .out1(demultiplexer_2_out1), .out2(demultiplexer_2_out2),
    .out3(demultiplexer_2_out3), .out4(demultiplexer_2_out4), .out5(demultiplexer_2_out5),
    .out6(demultiplexer_2_out6), .out7(demultiplexer_2_out7), .in(1'b1), .sel(RW[2:0]),
    .en(demultiplexer_1_out0));
  Demultiplexer #(.select(3), .disabled(0)) demultiplexer_3 (
    .out0(demultiplexer_3_out0), .out1(demultiplexer_3_out1), .out2(demultiplexer_3_out2),
    .out3(demultiplexer_3_out3), .out4(demultiplexer_3_out4), .out5(demultiplexer_3_out5),
    .out6(demultiplexer_3_out6), .out7(demultiplexer_3_out7), .in(1'b1), .sel(RW[2:0]),
    .en(demultiplexer_1_out1));
  Demultiplexer #(.select(3), .disabled(0)) demultiplexer_4 (
    .out0(demultiplexer_4_out0), .out1(demultiplexer_4_out1), .out2(demultiplexer_4_out2),
    .out3(demultiplexer_4_out3), .out4(demultiplexer_4_out4), .out5(demultiplexer_4_out5),
    .out6(demultiplexer_4_out6), .out7(demultiplexer_4_out7), .in(1'b1), .sel(RW[2:0]),
    .en(demultiplexer_1_out2));
  Demultiplexer #(.select(3), .disabled(0)) demultiplexer_5 (
    .out0(demultiplexer_5_out0), .out1(demultiplexer_5_out1), .out2(demultiplexer_5_out2),
    .out3(demultiplexer_5_out3), .out4(demultiplexer_5_out4), .out5(demultiplexer_5_out5),
    .out6(demultiplexer_5_out6), .out7(demultiplexer_5_out7), .in(1'b1), .sel(RW[2:0]),
    .en(demultiplexer_1_out3));
  Register #(.width(32), .Select("low")) _0__Zero (
    .D(Din), .en(demultiplexer_2_out0), .Q(_0__Zero_q));  // open: clk, clr
  Register #(.width(32), .Select("low")) _8__t0 (
    .D(Din), .en(demultiplexer_3_out0), .Q(_8__t0_q), .clk(clk));  // open: clr
  Register #(.width(32), .Select("low")) _16__s0 (.D(Din), .en(demultiplexer_4_out0), .Q(s0), .clk(clk));  // open: clr
  Register #(.width(32), .Select("low")) _24__t8 (
    .D(Din), .en(demultiplexer_5_out0), .Q(_24__t8_q), .clk(clk));  // open: clr
  Register #(.width(32), .Select("low")) _1__at (
    .D(Din), .en(demultiplexer_2_out1), .Q(_1__at_q), .clk(clk));  // open: clr
  Register #(.width(32), .Select("low")) _9__t1 (
    .D(Din), .en(demultiplexer_3_out1), .Q(_9__t1_q), .clk(clk));  // open: clr
  Register #(.width(32), .Select("low")) _17__s1 (.D(Din), .en(demultiplexer_4_out1), .Q(s1), .clk(clk));  // open: clr
  Register #(.width(32), .Select("low")) _25__t9 (
    .D(Din), .en(demultiplexer_5_out1), .Q(_25__t9_q), .clk(clk));  // open: clr
  Register #(.width(32), .Select("low")) _2__v0 (.D(Din), .en(demultiplexer_2_out2), .Q(v0), .clk(clk));  // open: clr
  Register #(.width(32), .Select("low")) _10__t2 (
    .D(Din), .en(demultiplexer_3_out2), .Q(_10__t2_q), .clk(clk));  // open: clr
  Register #(.width(32), .Select("low")) _18__s2 (.D(Din), .en(demultiplexer_4_out2), .Q(s2), .clk(clk));  // open: clr
  Register #(.width(32), .Select("low")) _26__k0 (
    .D(Din), .en(demultiplexer_5_out2), .Q(_26__k0_q), .clk(clk));  // open: clr
  Register #(.width(32), .Select("low")) _3__v1 (
    .D(Din), .en(demultiplexer_2_out3), .Q(_3__v1_q), .clk(clk));  // open: clr
  Register #(.width(32), .Select("low")) _11__t3 (
    .D(Din), .en(demultiplexer_3_out3), .Q(_11__t3_q), .clk(clk));  // open: clr
  Register #(.width(32), .Select("low")) _19__s3 (
    .D(Din), .en(demultiplexer_4_out3), .Q(_19__s3_q), .clk(clk));  // open: clr
  Register #(.width(32), .Select("low")) _27__k1 (
    .D(Din), .en(demultiplexer_5_out3), .Q(_27__k1_q), .clk(clk));  // open: clr
  Register #(.width(32), .Select("low")) _4__a0 (.D(Din), .en(demultiplexer_2_out4), .Q(a0), .clk(clk));  // open: clr
  Register #(.width(32), .Select("low")) _12__t4 (
    .D(Din), .en(demultiplexer_3_out4), .Q(_12__t4_q), .clk(clk));  // open: clr
  Register #(.width(32), .Select("low")) _20__s4 (
    .D(Din), .en(demultiplexer_4_out4), .Q(_20__s4_q), .clk(clk));  // open: clr
  Register #(.width(32), .Select("low")) _28__gp (
    .D(Din), .en(demultiplexer_5_out4), .Q(_28__gp_q), .clk(clk));  // open: clr
  Register #(.width(32), .Select("low")) _5__a1 (
    .D(Din), .en(demultiplexer_2_out5), .Q(_5__a1_q), .clk(clk));  // open: clr
  Register #(.width(32), .Select("low")) _13__t5 (
    .D(Din), .en(demultiplexer_3_out5), .Q(_13__t5_q), .clk(clk));  // open: clr
  Register #(.width(32), .Select("low")) _21__s5 (
    .D(Din), .en(demultiplexer_4_out5), .Q(_21__s5_q), .clk(clk));  // open: clr
  Register #(.width(32), .Select("low")) _29__sp (
    .D(Din), .en(demultiplexer_5_out5), .Q(_29__sp_q), .clk(clk));  // open: clr
  Register #(.width(32), .Select("low")) _6__a2 (
    .D(Din), .en(demultiplexer_2_out6), .Q(_6__a2_q), .clk(clk));  // open: clr
  Register #(.width(32), .Select("low")) _14__t6 (
    .D(Din), .en(demultiplexer_3_out6), .Q(_14__t6_q), .clk(clk));  // open: clr
  Register #(.width(32), .Select("low")) _22__s6 (
    .D(Din), .en(demultiplexer_4_out6), .Q(_22__s6_q), .clk(clk));  // open: clr
  Register #(.width(32), .Select("low")) _30__fp (
    .D(Din), .en(demultiplexer_5_out6), .Q(_30__fp_q), .clk(clk));  // open: clr
  Register #(.width(32), .Select("low")) _7__a3 (
    .D(Din), .en(demultiplexer_2_out7), .Q(_7__a3_q), .clk(clk));  // open: clr
  Register #(.width(32), .Select("low")) _15__t7 (
    .D(Din), .en(demultiplexer_3_out7), .Q(_15__t7_q), .clk(clk));  // open: clr
  Register #(.width(32), .Select("low")) _23__s7 (
    .D(Din), .en(demultiplexer_4_out7), .Q(_23__s7_q), .clk(clk));  // open: clr
  Register #(.width(32), .Select("low")) _31__ra (.D(Din), .en(demultiplexer_5_out7), .Q(ra), .clk(clk));  // open: clr
  Multiplexer #(.select(5), .width(32), .enable("false")) multiplexer_1 (
    .in0(_0__Zero_q), .in1(_1__at_q), .in2(v0), .in3(_3__v1_q), .in4(a0), .in5(_5__a1_q), .in6(_6__a2_q),
    .in7(_7__a3_q), .in8(_8__t0_q), .in9(_9__t1_q), .in10(_10__t2_q), .in11(_11__t3_q), .in12(_12__t4_q),
    .in13(_13__t5_q), .in14(_14__t6_q), .in15(_15__t7_q), .in16(s0), .in17(s1), .in18(s2), .in19(_19__s3_q),
    .in20(_20__s4_q), .in21(_21__s5_q), .in22(_22__s6_q), .in23(_23__s7_q), .in24(_24__t8_q),
    .in25(_25__t9_q), .in26(_26__k0_q), .in27(_27__k1_q), .in28(_28__gp_q), .in29(_29__sp_q),
    .in30(_30__fp_q), .in31(ra), .out(R1), .sel(R1_num));
  Multiplexer #(.select(5), .width(32), .enable("false")) multiplexer_2 (
    .in0(_0__Zero_q), .in1(_1__at_q), .in2(v0), .in3(_3__v1_q), .in4(a0), .in5(_5__a1_q), .in6(_6__a2_q),
    .in7(_7__a3_q), .in8(_8__t0_q), .in9(_9__t1_q), .in10(_10__t2_q), .in11(_11__t3_q), .in12(_12__t4_q),
    .in13(_13__t5_q), .in14(_14__t6_q), .in15(_15__t7_q), .in16(s0), .in17(s1), .in18(s2), .in19(_19__s3_q),
    .in20(_20__s4_q), .in21(_21__s5_q), .in22(_22__s6_q), .in23(_23__s7_q), .in24(_24__t8_q),
    .in25(_25__t9_q), .in26(_26__k0_q), .in27(_27__k1_q), .in28(_28__gp_q), .in29(_29__sp_q),
    .in30(_30__fp_q), .in31(ra), .out(R2), .sel(R2_num));

  // Other names for the same wires on the sheet: reg1[31:0] = R1; reg1_num[4:0] = R1_num; reg2[31:0] = R2;
  //   reg2_num[4:0] = R2_num; write_data[31:0] = Din; write_reg_num[4:0] = RW

  // Notes on the sheet:
  //   Input
  //   Output
endmodule

module ULA (
  input  [31:0] A,
  input  [31:0] B,
  input  [4:0] SHIFT_AMOUNT,
  input  [5:0] OP,
  output igual,
  output [31:0] Resultado
);

  wire comparator_2_lt;
  wire [31:0] adder_1_out, AND_out, bit_extender_1_out, divider_1_out, multiplier_1_out, OR_out,
       shifter_1_out, shifter_2_out, subtractor_1_out;

  Adder #(.width(32)) adder_1 (.a(A), .b(B), .out(adder_1_out));  // open: cin, cout
  Subtractor #(.width(32)) subtractor_1 (.a(A), .b(B), .out(subtractor_1_out));  // open: bin, bout
  Multiplier #(.width(32)) multiplier_1 (.a(A), .b(B), .out(multiplier_1_out));  // open: cin, cout
  Divider #(.width(32)) divider_1 (.a(A), .b(B), .out(divider_1_out));  // open: upper, rem
  Comparator #(.width(32)) comparator_1 (.a(A), .b(B), .eq(igual));  // open: gt, lt
  assign AND_out = A & B;  // AND_Gate AND, 32 bits wide
  assign OR_out = A | B;  // OR_Gate OR, 32 bits wide
  Comparator #(.width(32)) comparator_2 (.a(A), .b(B), .lt(comparator_2_lt));  // open: gt, eq
  Shifter #(.width(32)) shifter_1 (.in(A), .\dist (SHIFT_AMOUNT), .out(shifter_1_out));
  Shifter #(.width(32), .shift("lr")) shifter_2 (.in(A), .\dist (SHIFT_AMOUNT), .out(shifter_2_out));
  assign bit_extender_1_out = {{31{1'b0}}, comparator_2_lt};  // Bit_Extender bit_extender_1
  Multiplexer #(.select(4), .width(32), .enable("false")) multiplexer_1 (
    .in0(adder_1_out), .in1(subtractor_1_out), .in2(multiplier_1_out), .in3(divider_1_out), .in4(AND_out),
    .in5(OR_out), .in6(bit_extender_1_out), .in7(shifter_1_out), .in8(shifter_2_out), .out(Resultado),
    .sel(OP[3:0]));  // open: in9, in10, in11, in12, in13, in14, in15

  // Notes on the sheet:
  //   SLT
  //   SLL
  //   SLR
endmodule

module UC (
  input  UC5,
  input  UC4,
  input  UC3,
  input  UC2,
  input  UC1,
  input  UC0,
  output REGDEST,
  output JUMP,
  output BRANCH,
  output MEMTOREG,
  output ULA0P0,
  output ULA0P1,
  output ULAOPSRC,
  output MEM_WR,
  output ULASRC,
  output WR,
  output JR
);

  wire and_1_out, and_2_out, and_3_out, and_5_out, and_6_out, and_8_out, and_9_out, and_10_out, and_11_out,
       and_12_out, and_13_out, and_14_out, and_15_out, and_16_out, and_17_out, and_18_out, and_19_out,
       and_20_out, and_21_out, and_22_out, and_23_out, and_24_out, and_25_out, and_26_out, and_27_out,
       and_28_out, and_29_out, and_30_out, and_31_out, and_32_out, and_33_out, and_34_out, and_35_out,
       and_36_out, and_37_out, and_38_out, and_39_out, and_40_out, and_41_out, and_42_out, and_43_out,
       and_44_out, and_45_out, and_46_out, and_47_out, and_48_out, and_49_out, and_50_out, and_51_out,
       and_52_out, and_53_out, not_1_out, not_2_out, not_3_out, not_4_out, not_5_out, not_6_out, not_7_out,
       not_8_out, not_9_out, not_10_out, not_11_out, not_12_out, not_13_out, not_14_out, not_15_out,
       not_16_out, not_17_out, not_18_out, not_19_out, not_20_out, not_21_out, not_22_out, not_23_out,
       not_24_out, not_25_out, not_26_out, not_27_out, not_28_out, not_29_out, not_30_out, not_31_out,
       not_32_out, not_33_out, not_34_out, not_35_out, not_36_out, not_37_out, not_38_out, not_39_out,
       not_40_out, not_41_out, not_42_out, not_43_out, not_44_out, not_45_out, not_46_out, not_47_out,
       not_48_out, not_49_out, not_50_out, not_51_out, not_52_out, not_53_out, not_54_out, not_55_out,
       not_56_out, not_57_out, not_58_out, not_59_out, not_60_out, not_61_out, not_62_out, not_63_out,
       not_64_out, not_65_out, not_66_out, not_67_out, not_68_out, not_69_out, not_70_out, not_71_out,
       not_72_out, not_73_out, not_74_out, not_75_out, not_76_out, not_77_out, not_78_out, not_79_out;

  not not_1 (not_1_out, UC3);
  not not_2 (not_2_out, UC2);
  not not_3 (not_3_out, UC1);
  not not_4 (not_4_out, UC0);
  not not_5 (not_5_out, UC1);
  not not_6 (not_6_out, UC5);
  not not_7 (not_7_out, UC4);
  not not_8 (not_8_out, UC2);
  not not_9 (not_9_out, UC5);
  not not_10 (not_10_out, UC4);
  not not_11 (not_11_out, UC3);
  not not_12 (not_12_out, UC1);
  not not_13 (not_13_out, UC5);
  not not_14 (not_14_out, UC4);
  not not_15 (not_15_out, UC2);
  not not_16 (not_16_out, UC1);
  not not_17 (not_17_out, UC5);
  not not_18 (not_18_out, UC4);
  not not_19 (not_19_out, UC3);
  not not_20 (not_20_out, UC3);
  not not_21 (not_21_out, UC0);
  not not_22 (not_22_out, UC3);
  not not_23 (not_23_out, UC1);
  not not_24 (not_24_out, UC1);
  not not_25 (not_25_out, UC0);
  not not_26 (not_26_out, UC0);
  not not_27 (not_27_out, UC1);
  not not_28 (not_28_out, UC0);
  not not_29 (not_29_out, UC1);
  not not_30 (not_30_out, UC3);
  not not_31 (not_31_out, UC2);
  not not_32 (not_32_out, UC3);
  not not_33 (not_33_out, UC1);
  not not_34 (not_34_out, UC5);
  not not_35 (not_35_out, UC4);
  not not_36 (not_36_out, UC1);
  not not_37 (not_37_out, UC2);
  not not_38 (not_38_out, UC1);
  not not_39 (not_39_out, UC2);
  not not_40 (not_40_out, UC1);
  not not_41 (not_41_out, UC3);
  not not_42 (not_42_out, UC1);
  not not_43 (not_43_out, UC3);
  not not_44 (not_44_out, UC2);
  not not_45 (not_45_out, UC3);
  not not_46 (not_46_out, UC1);
  not not_47 (not_47_out, UC2);
  not not_48 (not_48_out, UC1);
  not not_49 (not_49_out, UC2);
  not not_50 (not_50_out, UC1);
  not not_51 (not_51_out, UC0);
  not not_52 (not_52_out, UC3);
  not not_53 (not_53_out, UC2);
  not not_54 (not_54_out, UC3);
  not not_55 (not_55_out, UC3);
  not not_56 (not_56_out, UC0);
  not not_57 (not_57_out, UC5);
  not not_58 (not_58_out, UC4);
  not not_59 (not_59_out, UC2);
  not not_60 (not_60_out, UC1);
  not not_61 (not_61_out, UC0);
  not not_62 (not_62_out, UC5);
  not not_63 (not_63_out, UC4);
  not not_64 (not_64_out, UC3);
  not not_65 (not_65_out, UC2);
  not not_66 (not_66_out, UC5);
  not not_67 (not_67_out, UC4);
  not not_68 (not_68_out, UC3);
  not not_69 (not_69_out, UC0);
  not not_70 (not_70_out, UC5);
  not not_71 (not_71_out, UC4);
  not not_72 (not_72_out, UC3);
  not not_73 (not_73_out, UC5);
  not not_74 (not_74_out, UC4);
  not not_75 (not_75_out, UC2);
  not not_76 (not_76_out, UC5);
  not not_77 (not_77_out, UC4);
  not not_78 (not_78_out, UC1);
  not not_79 (not_79_out, UC0);
  and and_1 (and_1_out, not_1_out, not_2_out, not_3_out, not_4_out);
  and and_2 (and_2_out, UC2, not_5_out, UC0);
  and and_3 (and_3_out, UC3, UC2, UC1);
  and and_4 (JUMP, not_6_out, not_7_out, UC3, not_8_out, UC1);
  and and_5 (and_5_out, not_9_out, not_10_out, not_11_out, UC2, not_12_out, UC0);
  and and_6 (and_6_out, not_13_out, not_14_out, UC3, not_15_out, not_16_out, UC0);
  and and_7 (MEMTOREG, not_17_out, not_18_out, not_19_out, UC2, UC1, UC0);
  and and_8 (and_8_out, not_20_out, UC1, not_21_out);
  and and_9 (and_9_out, not_22_out, UC2, not_23_out);
  and and_10 (and_10_out, UC2, not_24_out, UC0);
  and and_11 (and_11_out, UC2, UC1, not_25_out);
  and and_12 (and_12_out, UC4, UC1, not_26_out);
  and and_13 (and_13_out, UC4, UC2, not_27_out);
  and and_14 (and_14_out, UC5, UC1, not_28_out);
  and and_15 (and_15_out, UC5, UC2, not_29_out);
  and and_16 (and_16_out, not_30_out, not_31_out, UC1, UC0);
  and and_17 (and_17_out, not_32_out, UC2, not_33_out);
  and and_18 (and_18_out, not_34_out, not_35_out, UC3, not_36_out, UC0);
  and and_19 (and_19_out, UC4, not_37_out, UC1, UC0);
  and and_20 (and_20_out, UC4, UC2, not_38_out);
  and and_21 (and_21_out, UC5, not_39_out, UC1, UC0);
  and and_22 (and_22_out, UC5, UC2, not_40_out);
  and and_23 (and_23_out, not_41_out, UC0);
  and and_24 (and_24_out, not_42_out, UC0);
  and and_25 (and_25_out, not_43_out, not_44_out, UC1);
  and and_26 (and_26_out, not_45_out, UC2, not_46_out);
  and and_27 (and_27_out, UC3, not_47_out, not_48_out);
  and and_28 (and_28_out, UC3, UC2, UC1);
  and and_29 (and_29_out, UC4, UC2);
  and and_30 (and_30_out, UC4, UC3);
  and and_31 (and_31_out, UC5, UC1);
  and and_32 (and_32_out, UC5, UC2);
  and and_33 (and_33_out, UC3, not_49_out, not_50_out, not_51_out);
  and and_34 (and_34_out, UC3, UC2, UC0);
  and and_35 (and_35_out, UC3, UC2, UC1);
  and and_36 (and_36_out, UC4, UC3);
  and and_37 (and_37_out, UC5, UC3);
  and and_38 (and_38_out, not_52_out, not_53_out, UC0);
  and and_39 (and_39_out, not_54_out, UC1);
  and and_40 (and_40_out, not_55_out, UC2, not_56_out);
  and and_41 (and_41_out, UC2, UC1);
  and and_42 (and_42_out, not_57_out, not_58_out, UC3, not_59_out, not_60_out, not_61_out);
  and and_43 (and_43_out, UC3, UC2, UC0);
  and and_44 (and_44_out, UC4, UC0);
  and and_45 (and_45_out, UC4, UC1);
  and and_46 (and_46_out, UC4, UC2);
  and and_47 (and_47_out, UC5, UC0);
  and and_48 (and_48_out, UC5, UC1);
  and and_49 (and_49_out, UC5, UC2);
  and and_50 (and_50_out, not_62_out, not_63_out, not_64_out, not_65_out);
  and and_51 (and_51_out, not_66_out, not_67_out, not_68_out, not_69_out);
  and and_52 (and_52_out, not_70_out, not_71_out, not_72_out, UC1);
  and and_53 (and_53_out, not_73_out, not_74_out, not_75_out, UC1, UC0);
  and and_54 (JR, not_76_out, not_77_out, UC3, UC2, not_78_out, not_79_out);
  or or_1 (REGDEST, and_1_out, and_2_out, and_3_out, UC4, UC5);
  or or_2 (BRANCH, and_5_out, and_6_out);
  or or_3 (ULA0P0, and_8_out, and_9_out, and_10_out, and_11_out, and_12_out, and_13_out, and_14_out, and_15_out);
  or or_4 (ULA0P1, and_16_out, and_17_out, and_18_out, and_19_out, and_20_out, and_21_out, and_22_out);
  or or_5 (ULAOPSRC, and_23_out, and_24_out, and_25_out, and_26_out, and_27_out, and_28_out, and_29_out, and_30_out, and_31_out, and_32_out);
  or or_6 (MEM_WR, and_33_out, and_34_out, and_35_out, and_36_out, and_37_out);
  or or_7 (WR, and_50_out, and_51_out, and_52_out, and_53_out);
  or or_8 (ULASRC, and_38_out, and_39_out, and_40_out, and_41_out, and_42_out, and_43_out, and_44_out, and_45_out, and_46_out, and_47_out, and_48_out, and_49_out);
endmodule

// ULAOP
module OPULA (
  input  OPCOD0,
  input  OPCOD1,
  input  OPCOD2,
  input  OPCOD3,
  input  OPCOD4,
  input  OPCOD5,
  input  FUNC0,
  input  FUNC1,
  input  FUNC2,
  input  FUNC3,
  input  FUNC4,
  input  FUNC5,
  output ULAOP0,
  output ULAOP1,
  output ULAOP2,
  output ULAOP3
);
endmodule

// UC
module UC_W (
  input  [5:0] in_1,
  output REGDEST,
  output JUMP,
  output BRANCH,
  output MEMTOREG,
  output [2:0] ALUOP,
  output MEMWRITE,
  output ALUSRC,
  output REGWRITE,
  output JR
);

  UC uc_1 (
    .UC5(in_1[5]), .UC4(in_1[4]), .UC3(in_1[3]), .UC2(in_1[2]), .REGDEST(REGDEST), .UC1(in_1[1]),
    .UC0(in_1[0]), .JUMP(JUMP), .BRANCH(BRANCH), .MEMTOREG(MEMTOREG), .ULA0P0(ALUOP[0]), .ULA0P1(ALUOP[1]),
    .ULAOPSRC(ALUOP[2]), .MEM_WR(MEMWRITE), .ULASRC(ALUSRC), .WR(REGWRITE), .JR(JR));
endmodule

// ALUCONTROL
module ALU_CONTROL (
  input  [5:0] FUNC,
  input  [2:0] ALU_OP,
  output [5:0] ULA_OP
);

  wire [5:0] bit_extender_1_out, multiplexer_1_out;

  Multiplexer #(.select(2), .width(6), .enable("false")) multiplexer_1 (
    .in0(FUNC), .in1(6'b000110), .out(multiplexer_1_out), .sel(ALU_OP[1:0]));  // open: in2, in3
  // Probe on ALU_OP[1:0]
  assign bit_extender_1_out = {{4{1'b0}}, ALU_OP[1:0]};  // Bit_Extender bit_extender_1
  // Probe on multiplexer_1_out
  Multiplexer #(.width(6), .enable("false")) multiplexer_2 (
    .in0(multiplexer_1_out), .in1(bit_extender_1_out), .out(ULA_OP), .sel(ALU_OP[2]));
endmodule

module REG_IF_ID (
  input  [31:0] PC_4,
  input  [31:0] INSTRUCTION,
  input  in_3,
  input  CLK,
  output [31:0] PC_4_2,
  output [31:0] INSTRUCTION_2
);

  Register #(.width(32), .Select("low")) register_1 (.D(PC_4), .en(in_3), .Q(PC_4_2), .clk(CLK));  // open: clr
  Register #(.width(32), .Select("low")) register_2 (
    .D(INSTRUCTION), .en(in_3), .Q(INSTRUCTION_2), .clk(CLK));  // open: clr
endmodule

module REG_ID_EX (
  input  RegDest,
  input  Jump,
  input  Branch,
  input  MemtoReg,
  input  [2:0] ALUOp,
  input  MemWrite,
  input  ALUSrc,
  input  RegWrite,
  input  Jr,
  input  [25:0] LABEL,
  input  [31:0] PC_4,
  input  [31:0] DATA_RS,
  input  [31:0] DATA_RT,
  input  [31:0] IMEXT,
  input  [4:0] RS,
  input  [4:0] RT,
  input  [4:0] RD,
  input  [4:0] SHAMT,
  input  [5:0] FUNC,
  input  CLEAR,
  input  CLK,
  output RegDest_2,
  output Jump_2,
  output Branch_2,
  output MemtoReg_2,
  output [2:0] ALUOp_2,
  output MemWrite_2,
  output ALUSrc_2,
  output RegWrite_2,
  output Jr_2,
  output [25:0] LABEL_2,
  output [31:0] PC_4_2,
  output [31:0] DATA_RS_2,
  output [31:0] DATA_RT_2,
  output [31:0] IMEXT_2,
  output [4:0] RS_2,
  output [4:0] RT_2,
  output [4:0] RD_2,
  output [4:0] SHAMT_2,
  output [5:0] FUNC_2
);

  wire [10:0] multiplexer_1_out;

  Multiplexer #(.width(11), .enable("false")) multiplexer_1 (
    .in0({Jr, RegWrite, ALUSrc, MemWrite, ALUOp, MemtoReg, Branch, Jump, RegDest}), .in1({11{1'b0}}),
    .out(multiplexer_1_out), .sel(CLEAR));
  Register #(.width(1), .Select("low")) register_1 (
    .D(multiplexer_1_out[0]), .Q(RegDest_2), .clk(CLK));  // open: en, clr
  Register #(.width(1), .Select("low")) register_2 (.D(multiplexer_1_out[1]), .Q(Jump_2), .clk(CLK));  // open: en, clr
  Register #(.width(1), .Select("low")) register_3 (
    .D(multiplexer_1_out[2]), .Q(Branch_2), .clk(CLK));  // open: en, clr
  Register #(.width(1), .Select("low")) register_4 (
    .D(multiplexer_1_out[3]), .Q(MemtoReg_2), .clk(CLK));  // open: en, clr
  Register #(.width(3), .Select("low")) register_5 (
    .D(multiplexer_1_out[6:4]), .Q(ALUOp_2), .clk(CLK));  // open: en, clr
  Register #(.width(1), .Select("low")) register_6 (
    .D(multiplexer_1_out[7]), .Q(MemWrite_2), .clk(CLK));  // open: en, clr
  Register #(.width(1), .Select("low")) register_7 (
    .D(multiplexer_1_out[8]), .Q(ALUSrc_2), .clk(CLK));  // open: en, clr
  Register #(.width(1), .Select("low")) register_8 (
    .D(multiplexer_1_out[9]), .Q(RegWrite_2), .clk(CLK));  // open: en, clr
  Register #(.width(1), .Select("low")) register_9 (.D(multiplexer_1_out[10]), .Q(Jr_2), .clk(CLK));  // open: en, clr
  Register #(.width(26), .Select("low")) register_10 (.D(LABEL), .Q(LABEL_2), .clk(CLK));  // open: en, clr
  Register #(.width(32), .Select("low")) register_11 (.D(PC_4), .Q(PC_4_2), .clk(CLK));  // open: en, clr
  Register #(.width(32), .Select("low")) register_12 (.D(DATA_RS), .Q(DATA_RS_2), .clk(CLK));  // open: en, clr
  Register #(.width(32), .Select("low")) register_13 (.D(DATA_RT), .Q(DATA_RT_2), .clk(CLK));  // open: en, clr
  Register #(.width(32), .Select("low")) register_14 (.D(IMEXT), .Q(IMEXT_2), .clk(CLK));  // open: en, clr
  Register #(.width(5), .Select("low")) register_15 (.D(RS), .Q(RS_2), .clk(CLK));  // open: en, clr
  Register #(.width(5), .Select("low")) register_16 (.D(RT), .Q(RT_2), .clk(CLK));  // open: en, clr
  Register #(.width(5), .Select("low")) register_17 (.D(RD), .Q(RD_2), .clk(CLK));  // open: en, clr
  Register #(.width(5), .Select("low")) register_18 (.D(SHAMT), .Q(SHAMT_2), .clk(CLK));  // open: en, clr
  Register #(.width(6), .Select("low")) register_19 (.D(FUNC), .Q(FUNC_2), .clk(CLK));  // open: en, clr
endmodule

module REG_EX_MEM (
  input  BRANCH,
  input  MEMTOREG,
  input  [2:0] ALUOP,
  input  MEMORY_WRITE,
  input  REGWRITE,
  input  [31:0] BRANCH_ADDRESS,
  input  zero,
  input  [31:0] ALU_OUT,
  input  [31:0] DATA_RT,
  input  [4:0] WRITE_REGISTER,
  input  CLK,
  output BRANCH_2,
  output MEMTOREG_2,
  output [2:0] ALUOP_2,
  output MEMORY_WRITE_2,
  output REGWRITE_2,
  output [31:0] BRANCH_ADDRESS_2,
  output zero_2,
  output [31:0] ALU_OUT_2,
  output [31:0] DATA_RT_2,
  output [4:0] WRITE_REGISTER_2
);

  Register #(.width(1), .Select("low")) register_1 (.D(BRANCH), .Q(BRANCH_2), .clk(CLK));  // open: en, clr
  Register #(.width(1), .Select("low")) register_2 (.D(MEMTOREG), .Q(MEMTOREG_2), .clk(CLK));  // open: en, clr
  Register #(.width(3), .Select("low")) register_3 (.D(ALUOP), .Q(ALUOP_2), .clk(CLK));  // open: en, clr
  Register #(.width(1), .Select("low")) register_4 (.D(MEMORY_WRITE), .Q(MEMORY_WRITE_2), .clk(CLK));  // open: en, clr
  Register #(.width(1), .Select("low")) register_5 (.D(REGWRITE), .Q(REGWRITE_2), .clk(CLK));  // open: en, clr
  Register #(.width(32), .Select("low")) register_6 (
    .D(BRANCH_ADDRESS), .Q(BRANCH_ADDRESS_2), .clk(CLK));  // open: en, clr
  Register #(.width(1), .Select("low")) register_7 (.D(zero), .Q(zero_2), .clk(CLK));  // open: en, clr
  Register #(.width(32), .Select("low")) register_8 (.D(ALU_OUT), .Q(ALU_OUT_2), .clk(CLK));  // open: en, clr
  Register #(.width(32), .Select("low")) register_9 (.D(DATA_RT), .Q(DATA_RT_2), .clk(CLK));  // open: en, clr
  Register #(.width(5), .Select("low")) register_10 (
    .D(WRITE_REGISTER), .Q(WRITE_REGISTER_2), .clk(CLK));  // open: en, clr
endmodule

module REG_MEM_WB (
  input  REG_WRITE,
  input  MEMTOREG,
  input  [31:0] MEM_OUT,
  input  [31:0] ALU_OUT,
  input  [4:0] WRITE_REGISTER,
  input  CLK,
  output REG_WRITE_2,
  output MEMTOREG_2,
  output [31:0] MEM_OUT_2,
  output [31:0] ALU_OUT_2,
  output [4:0] WRITE_REGISTER_2
);

  Register #(.width(1), .Select("low")) register_1 (.D(REG_WRITE), .Q(REG_WRITE_2), .clk(CLK));  // open: en, clr
  Register #(.width(1), .Select("low")) register_2 (.D(MEMTOREG), .Q(MEMTOREG_2), .clk(CLK));  // open: en, clr
  Register #(.width(32), .Select("low")) register_3 (.D(MEM_OUT), .Q(MEM_OUT_2), .clk(CLK));  // open: en, clr
  Register #(.width(32), .Select("low")) register_4 (.D(ALU_OUT), .Q(ALU_OUT_2), .clk(CLK));  // open: en, clr
  Register #(.width(5), .Select("low")) register_5 (
    .D(WRITE_REGISTER), .Q(WRITE_REGISTER_2), .clk(CLK));  // open: en, clr
endmodule

module PC_SELECT (
  input  [31:0] PC_BRANCH,
  input  [31:0] PC_JUMP,
  input  [31:0] PC_JR,
  input  [31:0] PC_4,
  input  JR,
  input  JUMP,
  input  BRANCH,
  input  in_8,
  input  CLK,
  output [31:0] PC_4_2,
  output [15:0] _16_BITS
);

  wire and_1_out, and_2_out, and_3_out, and_4_out, not_1_out, not_2_out, not_3_out, not_4_out, not_5_out,
       not_6_out, not_7_out, not_8_out;
  wire [1:0] or_2_out;
  wire [31:0] multiplexer_1_out, register_1_q;

  not not_1 (not_1_out, BRANCH);
  not not_2 (not_2_out, JUMP);
  not not_3 (not_3_out, BRANCH);
  not not_4 (not_4_out, JR);
  not not_5 (not_5_out, BRANCH);
  not not_6 (not_6_out, JUMP);
  not not_7 (not_7_out, JUMP);
  not not_8 (not_8_out, JR);
  and and_1 (and_1_out, not_1_out, not_2_out, JR);
  and and_2 (and_2_out, not_3_out, JUMP, not_4_out);
  and and_3 (and_3_out, not_5_out, not_6_out, JR);
  and and_4 (and_4_out, BRANCH, not_7_out, not_8_out);
  or or_1 (or_2_out[1], and_1_out, and_2_out);
  or or_2 (or_2_out[0], and_3_out, and_4_out);
  Multiplexer #(.select(2), .width(32), .enable("false")) multiplexer_1 (
    .in0(PC_4), .in1(PC_BRANCH), .in2(PC_JUMP), .in3(PC_JR), .out(multiplexer_1_out), .sel(or_2_out));
  Register #(.width(32), .Select("low")) register_1 (
    .D(multiplexer_1_out), .en(in_8), .Q({register_1_q[31:18], _16_BITS, register_1_q[1:0]}), .clk(CLK));  // open: clr
  Adder #(.width(32)) adder_1 (
    .a({register_1_q[31:18], _16_BITS, register_1_q[1:0]}), .b(32'h4), .out(PC_4_2));  // open: cin, cout
  Register #(.width(32), .Select("low")) PC ();  // open: D, en, Q, clk, clr
endmodule

module INSTRUCTION_DECOMPOSITION (
  input  [31:0] in_1,
  output [5:0] OPCODE,
  output [25:0] LABEL,
  output [4:0] RS,
  output [4:0] RT,
  output [4:0] RS_2,
  output [4:0] RT_2,
  output [4:0] RD,
  output [4:0] SHAMT,
  output [5:0] FUNC,
  output [31:0] IMEXT
);

  assign IMEXT = {{16{1'b0}}, in_1[15:0]};  // Bit_Extender bit_extender_1

  assign FUNC = in_1[5:0];
  assign LABEL = in_1[25:0];
  assign OPCODE = in_1[31:26];
  assign RD = in_1[15:11];
  assign RS = in_1[25:21];
  assign RS_2 = in_1[25:21];
  assign RT = in_1[20:16];
  assign RT_2 = in_1[20:16];
  assign SHAMT = in_1[10:6];
endmodule

module WR_OUT_SELECT (
  input  JUMP,
  input  REG_DEST,
  input  [31:0] PC_4,
  input  [31:0] AUL_RESULT,
  input  [4:0] RT,
  input  [4:0] RD,
  output [31:0] ALU_OUT,
  output [4:0] WR_REGISTER
);

  Multiplexer #(.select(2), .width(5), .enable("false")) multiplexer_1 (
    .in0(RT), .in1(RD), .in2({5{1'b1}}), .out(WR_REGISTER), .sel({JUMP, REG_DEST}));  // open: in3
  Multiplexer #(.width(32), .enable("false")) multiplexer_2 (.in0(AUL_RESULT), .in1(PC_4), .out(ALU_OUT), .sel(JUMP));
endmodule

module PC_ENCODE (
  input  [25:0] LABEL,
  input  [31:0] PC_4,
  input  [31:0] IMEXT,
  output [31:0] JUMP_ADDRESS,
  output [31:0] BRANCH_ADDRESS
);

  wire [27:0] bit_extender_1_out;
  wire [31:0] shifter_2_out;

  assign bit_extender_1_out = {{2{1'b0}}, LABEL};  // Bit_Extender bit_extender_1
  Shifter #(.width(28)) shifter_1 (.in(bit_extender_1_out), .\dist (5'b00010), .out(JUMP_ADDRESS[27:0]));
  Shifter #(.width(32)) shifter_2 (.in(IMEXT), .\dist (5'b00010), .out(shifter_2_out));
  Adder #(.width(32)) adder_1 (.a(PC_4), .b(shifter_2_out), .out(BRANCH_ADDRESS));  // open: cin, cout

  assign JUMP_ADDRESS[31:28] = PC_4[31:28];
endmodule

module DECIDE_BRANCH (
  input  ZERO,
  input  [2:0] ALU_OP,
  input  BRANCH,
  output IS_BRANCH
);

  wire and_1_out, and_2_out, comparator_1_eq, comparator_2_eq;

  Comparator #(.width(3)) comparator_1 (.a(3'b111), .b(ALU_OP), .eq(comparator_1_eq));  // open: gt, lt
  Comparator #(.width(3)) comparator_2 (.a(3'b110), .b(ALU_OP), .eq(comparator_2_eq));  // open: gt, lt
  and and_1 (and_1_out, BRANCH, comparator_1_eq, ZERO);
  and and_2 (and_2_out, BRANCH, comparator_2_eq, ~ZERO);  // AND_Gate
  or or_1 (IS_BRANCH, and_1_out, and_2_out);
endmodule

module FORWARDING_UNIT (
  input  [4:0] IDEX_RT,
  input  [4:0] ID_EX_RS,
  input  [4:0] EX_MEM_RD,
  input  EX_MEM_REG_WRITE,
  input  [4:0] MEM_WB_RD,
  input  MEM_WB_REG_WRITE,
  output [1:0] FORWARD_A,
  output [1:0] FORWARD_B
);

  wire and_1_out, and_2_out, comparator_1_eq, comparator_2_eq, comparator_3_eq, comparator_4_eq, or_1_out,
       or_2_out, xor_1_out, xor_2_out;
  wire [1:0] and_4_out, and_6_out;

  or or_1 (or_1_out, EX_MEM_RD[0], EX_MEM_RD[1], EX_MEM_RD[2], EX_MEM_RD[3], EX_MEM_RD[4]);
  or or_2 (or_2_out, MEM_WB_RD[0], MEM_WB_RD[1], MEM_WB_RD[2], MEM_WB_RD[3], MEM_WB_RD[4]);
  and and_1 (and_1_out, or_1_out, EX_MEM_REG_WRITE);
  Comparator #(.width(5)) comparator_1 (.a(ID_EX_RS), .b(EX_MEM_RD), .eq(comparator_1_eq));  // open: gt, lt
  and and_2 (and_2_out, or_2_out, MEM_WB_REG_WRITE);
  Comparator #(.width(5)) comparator_2 (.a(ID_EX_RS), .b(MEM_WB_RD), .eq(comparator_2_eq));  // open: gt, lt
  Comparator #(.width(5)) comparator_3 (.a(EX_MEM_RD), .b(IDEX_RT), .eq(comparator_3_eq));  // open: gt, lt
  Comparator #(.width(5)) comparator_4 (.a(MEM_WB_RD), .b(IDEX_RT), .eq(comparator_4_eq));  // open: gt, lt
  and and_3 (and_4_out[1], comparator_1_eq, and_1_out);
  and and_4 (and_4_out[0], comparator_2_eq, and_2_out);
  and and_5 (and_6_out[1], and_1_out, comparator_3_eq);
  and and_6 (and_6_out[0], and_2_out, comparator_4_eq);
  Multiplexer #(.width(2), .enable("false")) multiplexer_1 (
    .in0(2'b00), .in1(and_4_out), .out(FORWARD_A), .sel(xor_1_out));
  xor xor_1 (xor_1_out, and_4_out[1], and_4_out[0]);
  xor xor_2 (xor_2_out, and_6_out[1], and_6_out[0]);
  Multiplexer #(.width(2), .enable("false")) multiplexer_2 (
    .in0(2'b00), .in1(and_6_out), .out(FORWARD_B), .sel(xor_2_out));
endmodule

module HAZARD_DETECTION_UNIT (
  input  [4:0] IFID_rt,
  input  [4:0] IFID_rs,
  input  [4:0] IDEX_rt,
  input  IDEX_MemRead,
  output ENABLE_PC,
  output ENABLE_IF_ID,
  output CLEAR_ID_EX
);

  wire comparator_1_eq, comparator_2_eq, or_1_out;

  not not_1 (ENABLE_PC, CLEAR_ID_EX);
  not not_2 (ENABLE_IF_ID, CLEAR_ID_EX);
  Comparator #(.width(5)) comparator_1 (.a(IDEX_rt), .b(IFID_rs), .eq(comparator_1_eq));  // open: gt, lt
  Comparator #(.width(5)) comparator_2 (.a(IDEX_rt), .b(IFID_rt), .eq(comparator_2_eq));  // open: gt, lt
  or or_1 (or_1_out, comparator_1_eq, comparator_2_eq);
  and and_1 (CLEAR_ID_EX, IDEX_MemRead, or_1_out);
endmodule

module FORWARDING_UNIT_2 (
  input  [31:0] R1,
  input  [31:0] R2,
  input  [4:0] RS,
  input  WR,
  input  [4:0] RT,
  input  [4:0] REG_DEST,
  input  [31:0] WRITE_DATA,
  output [31:0] DATA_RS,
  output [31:0] DATA_RT
);

  wire and_1_out, and_2_out, comparator_1_eq, comparator_2_eq;

  Comparator #(.width(5)) comparator_1 (.a(RS), .b(REG_DEST), .eq(comparator_1_eq));  // open: gt, lt
  Comparator #(.width(5)) comparator_2 (.a(REG_DEST), .b(RT), .eq(comparator_2_eq));  // open: gt, lt
  Multiplexer #(.width(32), .enable("false")) multiplexer_1 (
    .in0(R1), .in1(WRITE_DATA), .out(DATA_RS), .sel(and_1_out));
  and and_1 (and_1_out, comparator_1_eq, WR);
  and and_2 (and_2_out, comparator_2_eq, WR);
  Multiplexer #(.width(32), .enable("false")) multiplexer_2 (
    .in0(R2), .in1(WRITE_DATA), .out(DATA_RT), .sel(and_2_out));
endmodule

module ALU_MUX_CONTROL (
  input  ALU_SRC,
  input  [31:0] DATA_RS,
  input  [31:0] DATA_RT,
  input  [4:0] SHAMT,
  input  [31:0] IMEXT,
  input  [31:0] EX_MEM_RESULT,
  input  [1:0] FORWARD_A,
  input  [1:0] FORWARD_B,
  input  [31:0] MEM_WB_RESULT,
  output [31:0] A,
  output [31:0] B,
  output [4:0] SHIFT_AMOUNT,
  output [31:0] DATA_RT_2
);

  Multiplexer #(.select(2), .width(32), .enable("false")) multiplexer_1 (
    .in0(DATA_RS), .in1(MEM_WB_RESULT), .in2(EX_MEM_RESULT), .out(A), .sel(FORWARD_A));  // open: in3
  Multiplexer #(.select(2), .width(32), .enable("false")) multiplexer_2 (
    .in0(DATA_RT), .in1(MEM_WB_RESULT), .in2(EX_MEM_RESULT), .out(DATA_RT_2), .sel(FORWARD_B));  // open: in3
  Multiplexer #(.width(32), .enable("false")) multiplexer_3 (.in0(DATA_RT_2), .in1(IMEXT), .out(B), .sel(ALU_SRC));

  assign SHIFT_AMOUNT = SHAMT;
endmodule
